// Logisim project ESF.circ as structural Verilog
module S_box_0 (
  input  [3:0] in_1,
  output [3:0] out_2
);

  Multiplexer #(.select(4), .width(4), .enable("false")) multiplexer_1 (
    .in0(4'b0011), .in1(4'b1000), .in2(4'b1111), .in3(4'b0001), .in4(4'b1010), .in5(4'b0110), .in6(4'b0101),
    .in7(4'b1011), .in8(4'b1110), .in9(4'b1101), .in10(4'b0100), .in11(4'b0010), .in12(4'b0111),
    .in13(4'b0000), .in14(4'b1001), .in15(4'b1100), .out(out_2), .sel(in_1));
endmodule
